# Fritzing sketch Ultrasonic Diagram (saved by Fritzing 0.8.7b)
breadboards: 1

parts:
  ULTRASONIC_SENSORS = SRF05 Ultrasonic Rangefinder
  ARDUINO_NANO = Arduino Nano (Rev3.0)
  Part8 = SRF05 Ultrasonic Rangefinder
  Part9 = SRF05 Ultrasonic Rangefinder
  Part10 = SRF05 Ultrasonic Rangefinder
  Part11 = SRF05 Ultrasonic Rangefinder
  MOTOR4 = Vibration Motor
  MOTOR5 = Vibration Motor
  MOTOR6 = Vibration Motor
  MOTOR7 = Vibration Motor
  VIBRATING_MOTORS = Vibration Motor  # not connected

nets:
  VCC: ULTRASONIC_SENSORS.VCC, ARDUINO_NANO.5V, Part8.VCC, Part9.VCC, Part10.VCC, Part11.VCC
  N1: ULTRASONIC_SENSORS.Trig, ARDUINO_NANO.D2
  N2: ULTRASONIC_SENSORS.Echo, ARDUINO_NANO.D3
  GND: ULTRASONIC_SENSORS.GND, ARDUINO_NANO.GND, Part8.GND, Part9.GND, Part10.GND, Part11.GND, MOTOR4.NEG, MOTOR5.NEG, MOTOR6.NEG, MOTOR7.NEG
  N3: ARDUINO_NANO.D4, Part8.Trig
  N4: ARDUINO_NANO.D5, Part8.Echo
  N5: ARDUINO_NANO.D6, Part9.Trig
  N6: ARDUINO_NANO.D7, Part9.Echo
  N7: ARDUINO_NANO.D8, Part11.Trig
  N8: ARDUINO_NANO.D9, Part11.Echo
  N9: ARDUINO_NANO.D10, Part10.Trig
  N10: ARDUINO_NANO.D11/MOSI, Part10.Echo
  N11: ARDUINO_NANO.A3, MOTOR4.POS
  N12: ARDUINO_NANO.A2, MOTOR6.POS
  N13: ARDUINO_NANO.A1, MOTOR7.POS
  N14: ARDUINO_NANO.A0, MOTOR5.POS

custom parts:
  Vibration Motor: An eccentric vibration motor!
