# Fritzing sketch Wearable Sketch (saved by Fritzing 0.8.7b)
breadboards: 1

parts:
  Part15 = Lithium Ion Polymer Battery 3.7v 100mAh [part_number=1570]  # not connected
  Arduino_Nano = Arduino Nano (Rev3.0)
  MQ-7_Gas_sensor = GAS_SENSOR [package=mq-3]
  Flame_Sensor = KY-026
  Thermistor = LM35 Temperature Sensor [package="TO92 [THT]"]
  GSM+GPS_Shield = FONA 800 Shield
  S16 = Pushbutton [package="[THT]"]
  S17 = Pushbutton [package="[THT]"]
  LED11 = LED - 5mm [color="Green (555nm)" package="5 mm [THT]"]
  LED12 = LED - 5mm [color="Red (633nm)" package="5 mm [THT]"]
  R10 = Resistor [tolerance=±5% resistance=220 package=THT]
  R11 = Resistor [tolerance=±5% resistance=220 package=THT]
  SEN2 = Pulse Sensor [package=SIP]
  R12 = Resistor [tolerance=±5% resistance=220 package=THT]
  R13 = Resistor [tolerance=±5% resistance=220 package=THT]

nets:
  N1: Arduino_Nano.GND, Flame_Sensor.pin3, R10.Pin_0, R11.Pin_0, R12.Pin_0
  N2: Arduino_Nano.D2, MQ-7_Gas_sensor.H1
  N3: Arduino_Nano.D3, Thermistor.Vout
  N4: Arduino_Nano.D5, SEN2.Signal
  N5: Arduino_Nano.D7, GSM+GPS_Shield.RX
  N6: Arduino_Nano.D8, GSM+GPS_Shield.TX
  N7: Arduino_Nano.D9, GSM+GPS_Shield.RST
  VIN: Arduino_Nano.VIN, Flame_Sensor.pin2, GSM+GPS_Shield.GND, GSM+GPS_Shield.Pwr
  N8: Arduino_Nano.5V, Flame_Sensor.pin1
  N9: Arduino_Nano.A7, LED11.anode
  N10: Arduino_Nano.A6, LED12.anode
  N11: Arduino_Nano.A5, S17.Pin_3, S17.Pin_4
  N12: Arduino_Nano.A4, S16.Pin_3, S16.Pin_4
  N13: MQ-7_Gas_sensor.H2, Thermistor.+Vs, SEN2.Vcc
  GND: Thermistor.GND, SEN2.GND
  N14: S16.Pin_1, S16.Pin_2, R12.Pin_1
  N15: S17.Pin_1, S17.Pin_2, R13.Pin_1
  N16: LED11.cathode, R10.Pin_1
  N17: LED12.cathode, R11.Pin_1

custom parts:
  Lithium Ion Polymer Battery 3.7v 100mAh: Lithium ion polymer (also known as 'lipo' or 'lipoly') batteries are thin, light and powerful. The output ranges from 4.2V when completely charged to 3.7V. This battery has a capacity of ~100mAh for a total of about 0.4 Wh. The batteries come pre-attached with a genuine 2-pin JST-PH connector as shown and include the necessary protection circuitry.
  KY-026: ky-026 flame sensor module
  FONA 800 Shield: This shield fits on top of any classic Arduino or compatible, and packs a surprising amount of technology into it's little frame. At the heart is a GSM cellular module (we use the latest SIM800) the size of a postage stamp. Quad-band 850/900/1800/1900MHz - connect onto any global GSM network with any 2G SIM (in the USA, T-Mobile is suggested) Make and receive voice calls using a headset OR an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
  Pulse Sensor: Pulse Sensor Optical Heart Rate Monitor for Arduino and other microcontrollers
